# Fritzing sketch Buggy (saved by Fritzing 0.9.3b)
breadboards: 3

parts:
  IR_Left = 2E10 IR Infrared Sensor Module
  IR_Right = 2E10 IR Infrared Sensor Module
  Motor_controller = L293D [package=THT]
  Ultrasonic = hc-sr04
  Motor_Left = DC Motor
  Motor_Right = DC Motor
  Microcontroller = Arduino Nano 33 IOT

nets:
  3.3V: IR_Left.VCC, IR_Right.VCC, Ultrasonic.VCC, Microcontroller.3V3
  GND: IR_Left.GND, IR_Right.GND, Motor_controller.0V, Ultrasonic.GND, Microcontroller.GND
  N1: IR_Left.A0, Microcontroller.A7
  N2: IR_Right.A0, Microcontroller.A1
  N3: Motor_controller.Enable_1, Microcontroller.D12~/MISO
  N4: Motor_controller.In_1, Microcontroller.D11/MOSI
  N5: Motor_controller.Out_1_(_Controlled_by_Enable_1_), Motor_Left.pin_1
  N6: Motor_controller.Out_2_(_Controlled_by_Enable_1_), Motor_Left.pin_2
  N7: Motor_controller.In_2, Microcontroller.D10~
  5V: Motor_controller.+Vmotor, Motor_controller.+V, Microcontroller.+5V
  N8: Motor_controller.Enable_2, Microcontroller.D9~
  N9: Motor_controller.In_3, Microcontroller.D8
  N10: Motor_controller.Out_3_(_Controlled_by_Enable_2_), Motor_Right.pin_2
  N11: Motor_controller.Out_4_(_Controlled_by_Enable_2_), Motor_Right.pin_1
  N12: Motor_controller.In_4, Microcontroller.D7
  N13: Ultrasonic.Trig, Microcontroller.D2
  N14: Ultrasonic.Echo, Microcontroller.D3~

custom parts:
  2E10 IR Infrared Sensor Module: An infrared obstacle detector, with analogue & digital output
  hc-sr04: This is a HC-SR04 Distance Sensor
  Arduino Nano 33 IOT: The Arduino Nano 33 IoT is the easiest and cheapest point of entry to enhance existing devices (and creating new ones) to be part of the IoT and designing pico-network applications. Whether you are looking at building a sensor network connected to your office or home router, or if you want to create a BLE device sending data to a cellphone, the Nano 33 IoT is your one-stop-solution for many of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
